// Logisim project DataCache.circ as structural Verilog: 1 circuit, main circuit main
module main (
  input  [31:0] Address,
  input  Store,
  input  [31:0] Data_in,
  output [1:0] Byte_offset,
  output HIT_MISS,
  output [31:0] Data_Output
);

  wire Clock_out, comparator_1_eq, not_1_out, not_2_out, not_3_out, not_4_out, ram_1_data;
  wire [19:0] ram_2_data;

  Clock Clock (.out(Clock_out));
  not not_1 (not_1_out, Store);
  not not_2 (not_2_out, not_1_out);
  RAM #(.addrWidth(10), .dataWidth(1), .bus("separate")) ram_1 (
    .addr(Address[11:2]), .din(not_2_out), .data(ram_1_data), .str(not_2_out), .clk(Clock_out), .ld(not_1_out));  // open: sel, clr
  and and_1 (HIT_MISS, ram_1_data, comparator_1_eq);
  not not_3 (not_3_out, not_1_out);
  RAM #(.addrWidth(10), .dataWidth(20), .bus("separate")) ram_2 (
    .addr(Address[11:2]), .din(Address[31:12]), .data(ram_2_data), .str(not_3_out), .clk(Clock_out),
    .ld(not_1_out));  // open: sel, clr
  Comparator #(.width(20)) comparator_1 (.a(ram_2_data), .b(Address[31:12]), .eq(comparator_1_eq));  // open: gt, lt
  not not_4 (not_4_out, not_1_out);
  RAM #(.addrWidth(10), .dataWidth(32), .bus("separate")) ram_3 (
    .addr(Address[11:2]), .din(Data_in), .data(Data_Output), .str(not_4_out), .clk(Clock_out), .ld(not_1_out));  // open: sel, clr

  assign Byte_offset = Address[1:0];

  // Notes on the sheet:
  //   0 = Load
  //   1 = Store
  //   Tag
  //   Index
  //   VALID
  //   TAG
  //   DATA
endmodule
