// Logisim project Decode.circ as structural Verilog: 2 circuits, main circuit main
// 5
module main (
  input  ALUSrc,
  input  [31:0] instruction,
  input  RegDst,
  input  RegWrite,
  input  [31:0] write_back_data,
  output [31:0] shift_left_2,
  output [31:0] ALU_input_1,
  output [5:0] control,
  output [31:0] ALU_input_2,
  output [31:0] data_memory__write_data,
  output [5:0] ALU_Control
);

  wire [4:0] multiplexer_1_out;

  Multiplexer #(.width(5), .enable("false")) multiplexer_1 (
    .in0(instruction[20:16]), .in1(instruction[15:11]), .out(multiplexer_1_out), .sel(RegDst));
  registerFile registerfile_1 (
    .read_register_1(instruction[25:21]), .read_register_2(instruction[20:16]),
    .write_register(multiplexer_1_out), .write_data(write_back_data), .Reg_Write(RegWrite),
    .read_data_1(ALU_input_1), .read_data_2(data_memory__write_data));
  assign shift_left_2 = {{16{instruction[15]}}, instruction[15:0]};  // Bit_Extender bit_extender_1
  Multiplexer #(.width(32), .enable("false")) multiplexer_2 (
    .in0(data_memory__write_data), .in1(shift_left_2), .out(ALU_input_2), .sel(ALUSrc));

  assign ALU_Control = instruction[5:0];
  assign control = instruction[31:26];
endmodule

module registerFile (
  input  [4:0] read_register_1,
  input  [4:0] read_register_2,
  input  [4:0] write_register,
  input  [31:0] write_data,
  input  Reg_Write,
  output [31:0] read_data_1,
  output [31:0] read_data_2
);

  wire and_1_out, and_2_out, and_3_out, and_4_out, and_5_out, and_6_out, and_7_out, and_8_out, and_9_out,
       and_10_out, and_11_out, and_12_out, and_13_out, and_14_out, and_15_out, and_16_out, and_17_out,
       and_18_out, and_19_out, and_20_out, and_21_out, and_22_out, and_23_out, and_24_out, and_25_out,
       and_26_out, and_27_out, and_28_out, and_29_out, and_30_out, and_31_out, and_32_out, Clock_out,
       decoder_1_out0, decoder_1_out1, decoder_1_out2, decoder_1_out3, decoder_1_out4, decoder_1_out5,
       decoder_1_out6, decoder_1_out7, decoder_1_out8, decoder_1_out9, decoder_1_out10, decoder_1_out11,
       decoder_1_out12, decoder_1_out13, decoder_1_out14, decoder_1_out15, decoder_1_out16, decoder_1_out17,
       decoder_1_out18, decoder_1_out19, decoder_1_out20, decoder_1_out21, decoder_1_out22, decoder_1_out23,
       decoder_1_out24, decoder_1_out25, decoder_1_out26, decoder_1_out27, decoder_1_out28, decoder_1_out29,
       decoder_1_out30, decoder_1_out31;
  wire [31:0] a0_q, a1_q, a2_q, a3_q, at_q, fp_q, gp_q, k0_q, k1_q, ra_q, s0_q, s1_q, s2_q, s3_q, s4_q, s5_q,
       s6_q, s7_q, sp_q, t0_q, t1_q, t2_q, t3_q, t4_q, t5_q, t6_q, t7_q, t8_q, t9_q, v0_q, v1_q, zero_q;

  Decoder #(.select(5), .enable("false")) decoder_1 (
    .out0(decoder_1_out0), .out1(decoder_1_out1), .out2(decoder_1_out2), .out3(decoder_1_out3),
    .out4(decoder_1_out4), .out5(decoder_1_out5), .out6(decoder_1_out6), .out7(decoder_1_out7),
    .out8(decoder_1_out8), .out9(decoder_1_out9), .out10(decoder_1_out10), .out11(decoder_1_out11),
    .out12(decoder_1_out12), .out13(decoder_1_out13), .out14(decoder_1_out14), .out15(decoder_1_out15),
    .out16(decoder_1_out16), .out17(decoder_1_out17), .out18(decoder_1_out18), .out19(decoder_1_out19),
    .out20(decoder_1_out20), .out21(decoder_1_out21), .out22(decoder_1_out22), .out23(decoder_1_out23),
    .out24(decoder_1_out24), .out25(decoder_1_out25), .out26(decoder_1_out26), .out27(decoder_1_out27),
    .out28(decoder_1_out28), .out29(decoder_1_out29), .out30(decoder_1_out30), .out31(decoder_1_out31),
    .sel(write_register));
  buf and_1 (and_1_out, Reg_Write);  // AND_Gate
  and and_2 (and_2_out, decoder_1_out1, Reg_Write);
  and and_3 (and_3_out, decoder_1_out2, Reg_Write);
  and and_4 (and_4_out, decoder_1_out3, Reg_Write);
  and and_5 (and_5_out, decoder_1_out4, Reg_Write);
  and and_6 (and_6_out, decoder_1_out5, Reg_Write);
  and and_7 (and_7_out, decoder_1_out6, Reg_Write);
  and and_8 (and_8_out, decoder_1_out7, Reg_Write);
  and and_9 (and_9_out, decoder_1_out8, Reg_Write);
  and and_10 (and_10_out, decoder_1_out9, Reg_Write);
  and and_11 (and_11_out, decoder_1_out10, Reg_Write);
  and and_12 (and_12_out, decoder_1_out11, Reg_Write);
  and and_13 (and_13_out, decoder_1_out12, Reg_Write);
  and and_14 (and_14_out, decoder_1_out13, Reg_Write);
  and and_15 (and_15_out, decoder_1_out14, Reg_Write);
  and and_16 (and_16_out, decoder_1_out15, Reg_Write);
  Clock Clock (.out(Clock_out));
  Register #(.width(32)) zero (.Q(zero_q), .clk(Clock_out), .clr(and_1_out));  // open: D, en
  Register #(.width(32)) at (.D(write_data), .Q(at_q), .clk(Clock_out), .clr(and_2_out));  // open: en
  Register #(.width(32)) v0 (.D(write_data), .Q(v0_q), .clk(Clock_out), .clr(and_3_out));  // open: en
  Register #(.width(32)) v1 (.D(write_data), .Q(v1_q), .clk(Clock_out), .clr(and_4_out));  // open: en
  Register #(.width(32)) a0 (.D(write_data), .Q(a0_q), .clk(Clock_out), .clr(and_5_out));  // open: en
  Register #(.width(32)) a1 (.D(write_data), .Q(a1_q), .clk(Clock_out), .clr(and_6_out));  // open: en
  Register #(.width(32)) a2 (.D(write_data), .Q(a2_q), .clk(Clock_out), .clr(and_7_out));  // open: en
  Register #(.width(32)) a3 (.D(write_data), .Q(a3_q), .clk(Clock_out), .clr(and_8_out));  // open: en
  Register #(.width(32)) t0 (.D(write_data), .Q(t0_q), .clk(Clock_out), .clr(and_9_out));  // open: en
  Register #(.width(32)) t1 (.D(write_data), .Q(t1_q), .clk(Clock_out), .clr(and_10_out));  // open: en
  Register #(.width(32)) t2 (.D(write_data), .Q(t2_q), .clk(Clock_out), .clr(and_11_out));  // open: en
  Register #(.width(32)) t3 (.D(write_data), .Q(t3_q), .clk(Clock_out), .clr(and_12_out));  // open: en
  Register #(.width(32)) t4 (.D(write_data), .Q(t4_q), .clk(Clock_out), .clr(and_13_out));  // open: en
  Register #(.width(32)) t5 (.D(write_data), .Q(t5_q), .clk(Clock_out), .clr(and_14_out));  // open: en
  Register #(.width(32)) t6 (.D(write_data), .Q(t6_q), .clk(Clock_out), .clr(and_15_out));  // open: en
  Register #(.width(32)) t7 (.D(write_data), .Q(t7_q), .clk(Clock_out), .clr(and_16_out));  // open: en
  and and_17 (and_17_out, decoder_1_out16, Reg_Write);
  and and_18 (and_18_out, decoder_1_out17, Reg_Write);
  and and_19 (and_19_out, decoder_1_out18, Reg_Write);
  and and_20 (and_20_out, decoder_1_out19, Reg_Write);
  and and_21 (and_21_out, decoder_1_out20, Reg_Write);
  and and_22 (and_22_out, decoder_1_out21, Reg_Write);
  and and_23 (and_23_out, decoder_1_out22, Reg_Write);
  and and_24 (and_24_out, decoder_1_out23, Reg_Write);
  and and_25 (and_25_out, decoder_1_out24, Reg_Write);
  and and_26 (and_26_out, decoder_1_out25, Reg_Write);
  and and_27 (and_27_out, decoder_1_out26, Reg_Write);
  and and_28 (and_28_out, decoder_1_out27, Reg_Write);
  and and_29 (and_29_out, decoder_1_out28, Reg_Write);
  and and_30 (and_30_out, decoder_1_out29, Reg_Write);
  and and_31 (and_31_out, decoder_1_out30, Reg_Write);
  and and_32 (and_32_out, decoder_1_out31, Reg_Write);
  Register #(.width(32)) s0 (.D(write_data), .Q(s0_q), .clk(Clock_out), .clr(and_17_out));  // open: en
  Register #(.width(32)) s1 (.D(write_data), .Q(s1_q), .clk(Clock_out), .clr(and_18_out));  // open: en
  Register #(.width(32)) s2 (.D(write_data), .Q(s2_q), .clk(Clock_out), .clr(and_19_out));  // open: en
  Register #(.width(32)) s3 (.D(write_data), .Q(s3_q), .clk(Clock_out), .clr(and_20_out));  // open: en
  Register #(.width(32)) s4 (.D(write_data), .Q(s4_q), .clk(Clock_out), .clr(and_21_out));  // open: en
  Register #(.width(32)) s5 (.D(write_data), .Q(s5_q), .clk(Clock_out), .clr(and_22_out));  // open: en
  Register #(.width(32)) s6 (.D(write_data), .Q(s6_q), .clk(Clock_out), .clr(and_23_out));  // open: en
  Register #(.width(32)) s7 (.D(write_data), .Q(s7_q), .clk(Clock_out), .clr(and_24_out));  // open: en
  Register #(.width(32)) t8 (.D(write_data), .Q(t8_q), .clk(Clock_out), .clr(and_25_out));  // open: en
  Register #(.width(32)) t9 (.D(write_data), .Q(t9_q), .clk(Clock_out), .clr(and_26_out));  // open: en
  Register #(.width(32)) k0 (.D(write_data), .Q(k0_q), .clk(Clock_out), .clr(and_27_out));  // open: en
  Register #(.width(32)) k1 (.D(write_data), .Q(k1_q), .clk(Clock_out), .clr(and_28_out));  // open: en
  Register #(.width(32)) gp (.D(write_data), .Q(gp_q), .clk(Clock_out), .clr(and_29_out));  // open: en
  Register #(.width(32)) sp (.D(write_data), .Q(sp_q), .clk(Clock_out), .clr(and_30_out));  // open: en
  Register #(.width(32)) fp (.D(write_data), .Q(fp_q), .clk(Clock_out), .clr(and_31_out));  // open: en
  Register #(.width(32)) ra (.D(write_data), .Q(ra_q), .clk(Clock_out), .clr(and_32_out));  // open: en
  Multiplexer #(.select(5), .width(32), .enable("false")) multiplexer_1 (
    .in0(zero_q), .in1(at_q), .in2(v0_q), .in3(v1_q), .in4(a0_q), .in5(a1_q), .in6(a2_q), .in7(a3_q),
    .in8(t0_q), .in9(t1_q), .in10(t2_q), .in11(t3_q), .in12(t4_q), .in13(t5_q), .in14(t6_q), .in15(t7_q),
    .in16(s0_q), .in17(s1_q), .in18(s2_q), .in19(s3_q), .in20(s4_q), .in21(s5_q), .in22(s6_q), .in23(s7_q),
    .in24(t8_q), .in25(t9_q), .in26(k0_q), .in27(k1_q), .in28(gp_q), .in29(sp_q), .in30(fp_q), .in31(ra_q),
    .out(read_data_1), .sel(read_register_1));
  Multiplexer #(.select(5), .width(32), .enable("false")) multiplexer_2 (
    .in0(zero_q), .in1(at_q), .in2(v0_q), .in3(v1_q), .in4(a0_q), .in5(a1_q), .in6(a2_q), .in7(a3_q),
    .in8(t0_q), .in9(t1_q), .in10(t2_q), .in11(t3_q), .in12(t4_q), .in13(t5_q), .in14(t6_q), .in15(t7_q),
    .in16(s0_q), .in17(s1_q), .in18(s2_q), .in19(s3_q), .in20(s4_q), .in21(s5_q), .in22(s6_q), .in23(s7_q),
    .in24(t8_q), .in25(t9_q), .in26(k0_q), .in27(k1_q), .in28(gp_q), .in29(sp_q), .in30(fp_q), .in31(ra_q),
    .out(read_data_2), .sel(read_register_2));

  // Notes on the sheet:
  //   cannot write to register 0
endmodule
