// Logisim project FullCPU.circ as structural Verilog: 1 circuit, main circuit main
module main (
  input  Clock,
  input  [3:0] Core_ID,
  input  [4:0] Going_Out__Dest_ID,
  input  [31:0] Network_Input,
  output [31:0] Output_North,
  output [31:0] Output_South,
  output [31:0] Output_East,
  output [31:0] Output_West
);

  wire ALU_Control_sub, and_1_out, and_2_out, and_3_out, branch_out, comparator_1_eq, comparator_2_eq,
       comparator_3_eq, comparator_3_gt, comparator_3_lt, comparator_4_gt, comparator_4_lt,
       Control_Logic_alusrc, Control_Logic_beq, Control_Logic_bne, Control_Logic_jump, Control_Logic_memread,
       Control_Logic_memtoreg, Control_Logic_memwrite, Control_Logic_regdest, Control_Logic_regwrite,
       Data_Cache_hit_miss, Data_to_DC_out, Data_to_IC_out, Execute_zero_output, Instruction_Cache_hit_miss,
       OpCode_Generator_out, Send_Out_Packet_out, Stall_MemWrite_out, Stall_RegWrite_out, Stall_Signal_out;
  wire [1:0] Going_Out_ID_Found_out, multiplexer_8_out_3;
  wire [2:0] ALU_Control_alucntrl, multiplexer_1_out;
  wire [3:0] Control_Logic_aluop, multiplexer_2_out_2, register_1_q_2, register_1_q_4;
  wire [5:0] Decode_alu_control, Decode_control;
  wire [21:20] multiplexer_8_out_2;
  wire [26:0] register_1_q;
  wire [27:0] multiplexer_2_out, multiplexer_8_out;
  wire [31:0] Data_Cache_data_output, Decode_alu_input_1, Decode_alu_input_2, Decode_data_memory__write_data,
       Decode_shift_left_2, Execute_alu_result, Inst_Fetch_readaddress, Instruction_Cache_data_output,
       multiplexer_3_out, multiplexer_4_out, multiplexer_5_out, multiplexer_6_out, multiplexer_7_out;
  wire [31:31] register_1_q_3;

  Multiplexer #(.width(3), .enable("false")) multiplexer_1 (
    .in0(3'b001), .in1(3'b010), .out(multiplexer_1_out), .sel(OpCode_Generator_out));
  and Stall_MemWrite (Stall_MemWrite_out, ~Stall_Signal_out, Control_Logic_memwrite);  // AND_Gate
  or OpCode_Generator (OpCode_Generator_out, Control_Logic_regwrite, Control_Logic_memwrite);
  and Stall_RegWrite (Stall_RegWrite_out, ~Stall_Signal_out, Control_Logic_regwrite);  // AND_Gate
  Register #(.width(32)) register_1 (
    .D(Network_Input),
    .Q({register_1_q_3[31], register_1_q_2, register_1_q[26:24], register_1_q_4, register_1_q[19:0]}),
    .clk(Clock));  // open: en, clr
  or Stall_Signal (Stall_Signal_out, Instruction_Cache_hit_miss, Data_Cache_hit_miss);
  Multiplexer #(.width(32), .enable("false")) multiplexer_2 (
    .in0(Instruction_Cache_data_output),
    .in1({{5{1'b0}}, register_1_q[26:24], register_1_q_4, register_1_q[19:0]}),
    .out({multiplexer_2_out_2, multiplexer_2_out}), .sel(Data_to_IC_out));
  and and_1 (and_1_out, Execute_zero_output, branch_out);
  or branch (branch_out, Control_Logic_bne, Control_Logic_beq);
  InstFetch_main Inst_Fetch (
    .BranchAddress(Decode_shift_left_2), .JumpAddress(multiplexer_2_out), .Jump(Control_Logic_jump),
    .ReadAddress(Inst_Fetch_readaddress), .Branch(and_1_out), .Stall(Stall_Signal_out), .Clock(Clock));  // open: Reset
  and Data_to_IC (Data_to_IC_out, ~Data_Cache_hit_miss, Going_Out_ID_Found_out[1]);  // AND_Gate
  InstCache_main Instruction_Cache (
    .Address(Inst_Fetch_readaddress), .Data_Output(Instruction_Cache_data_output),
    .HIT_MISS(Instruction_Cache_hit_miss));  // open: Load, Byte_offset
  Comparator #(.width(4)) comparator_1 (.a(Core_ID), .b(register_1_q_2), .eq(comparator_1_eq));  // open: gt, lt
  Control_Logic Control_Logic (
    .Opcode(Decode_control), .Jump(Control_Logic_jump), .RegDest(Control_Logic_regdest),
    .BNE(Control_Logic_bne), .BEQ(Control_Logic_beq), .MemWrite(Control_Logic_memwrite),
    .MemRead(Control_Logic_memread), .MemToReg(Control_Logic_memtoreg), .RegWrite(Control_Logic_regwrite),
    .ALUSrc(Control_Logic_alusrc), .ALUOp(Control_Logic_aluop));  // open: R_Type, ExtOp
  and Going_Out_ID_Found (Going_Out_ID_Found_out[0], register_1_q_3[31], comparator_1_eq);
  and Reutrn_ID_Found (Going_Out_ID_Found_out[1], ~register_1_q_3[31], comparator_1_eq);  // AND_Gate
  Decode_main Decode (
    .ALUSrc(Control_Logic_alusrc), .instruction({multiplexer_2_out_2, multiplexer_2_out}),
    .control(Decode_control), .shift_left_2(Decode_shift_left_2), .ALU_Control(Decode_alu_control),
    .RegDst(Control_Logic_regdest), .write_back_data(multiplexer_5_out), .RegWrite(Stall_RegWrite_out),
    .ALU_input_1(Decode_alu_input_1), .ALU_input_2(Decode_alu_input_2),
    .data_memory__write_data(Decode_data_memory__write_data));
  or Send_Out_Packet (Send_Out_Packet_out, Instruction_Cache_hit_miss, Data_Cache_hit_miss);
  Multiplexer #(.width(32), .enable("false")) multiplexer_3 (
    .in0({Going_Out__Dest_ID, multiplexer_1_out, Core_ID, Inst_Fetch_readaddress[19:0]}),
    .in1({Going_Out__Dest_ID, multiplexer_1_out, Core_ID, Execute_alu_result[19:0]}),
    .out(multiplexer_3_out), .sel(Data_Cache_hit_miss));
  Multiplexer #(.width(32), .enable("false")) multiplexer_4 (
    .in0({32{1'b0}}), .in1(multiplexer_3_out), .out(multiplexer_4_out), .sel(Send_Out_Packet_out));
  ALU_Control ALU_Control (
    .MainCntrl(Control_Logic_aluop), .Funct(Decode_alu_control), .Sub(ALU_Control_sub),
    .ALUCntrl(ALU_Control_alucntrl));  // open: in_3
  ALU Execute (
    .A(Decode_alu_input_1), .B(Decode_alu_input_2), .Sub(ALU_Control_sub), .Opcode(ALU_Control_alucntrl),
    .ALU_Result(Execute_alu_result), .Zero_Output(Execute_zero_output));  // open: Slti_Output
  DataCache_main Data_Cache (
    .Store(Stall_MemWrite_out), .Address(Execute_alu_result), .Data_Output(Data_Cache_data_output),
    .HIT_MISS(Data_Cache_hit_miss), .Data_in(Decode_data_memory__write_data));  // open: Byte_offset
  Multiplexer #(.width(32), .enable("false")) multiplexer_5 (
    .in0(multiplexer_6_out), .in1(Execute_alu_result), .out(multiplexer_5_out), .sel(Control_Logic_memtoreg));
  Multiplexer #(.width(32), .enable("false")) multiplexer_6 (
    .in0(Data_Cache_data_output), .in1({{5{1'b0}}, register_1_q[26:24], register_1_q_4, register_1_q[19:0]}),
    .out(multiplexer_6_out), .sel(Data_to_DC_out));
  and Data_to_DC (Data_to_DC_out, Data_Cache_hit_miss, Going_Out_ID_Found_out[1]);
  Multiplexer #(.select(2), .width(32), .enable("false")) multiplexer_7 (
    .in0({register_1_q_3[31], register_1_q_2, register_1_q[26:24], register_1_q_4, register_1_q[19:0]}),
    .in1({32{1'b0}}),
    .in2({register_1_q_3[31], register_1_q_2, register_1_q[26:24], register_1_q_4, register_1_q[19:0]}),
    .in3({1'b0, register_1_q_4, {27{1'b0}}}), .out(multiplexer_7_out), .sel(Going_Out_ID_Found_out));
  Comparator #(.width(32)) comparator_2 (
    .a({register_1_q_3[31], register_1_q_2, register_1_q[26:24], register_1_q_4, register_1_q[19:0]}),
    .b({32{1'b0}}), .eq(comparator_2_eq));  // open: gt, lt
  // Probe on Control_Logic_memread
  Multiplexer #(.width(32), .enable("false")) multiplexer_8 (
    .in0(multiplexer_4_out), .in1(multiplexer_7_out),
    .out({multiplexer_8_out[27:20], multiplexer_8_out_3, multiplexer_8_out_2, multiplexer_8_out[19:0]}),
    .sel(comparator_2_eq));
  Comparator #(.width(2)) comparator_3 (
    .a(Core_ID[1:0]), .b(multiplexer_8_out_2), .gt(comparator_3_gt), .eq(comparator_3_eq),
    .lt(comparator_3_lt));
  Comparator #(.width(2)) comparator_4 (
    .a(multiplexer_8_out_3), .b(Core_ID[3:2]), .gt(comparator_4_gt), .lt(comparator_4_lt));  // open: eq
  Demultiplexer #(.width(32), .enable("false")) demultiplexer_1 (
    .out1(Output_South),
    .in({multiplexer_8_out[27:20], multiplexer_8_out_3, multiplexer_8_out_2, multiplexer_8_out[19:0]}),
    .sel(comparator_3_gt));  // open: out0
  Demultiplexer #(.width(32), .enable("false")) demultiplexer_2 (
    .out1(Output_North),
    .in({multiplexer_8_out[27:20], multiplexer_8_out_3, multiplexer_8_out_2, multiplexer_8_out[19:0]}),
    .sel(comparator_3_lt));  // open: out0
  and and_2 (and_2_out, comparator_3_eq, comparator_4_gt);
  and and_3 (and_3_out, comparator_3_eq, comparator_4_lt);
  Demultiplexer #(.width(32), .enable("false")) demultiplexer_3 (
    .out1(Output_East),
    .in({multiplexer_8_out[27:20], multiplexer_8_out_3, multiplexer_8_out_2, multiplexer_8_out[19:0]}),
    .sel(and_2_out));  // open: out0
  Demultiplexer #(.width(32), .enable("false")) demultiplexer_4 (
    .out1(Output_West),
    .in({multiplexer_8_out[27:20], multiplexer_8_out_3, multiplexer_8_out_2, multiplexer_8_out[19:0]}),
    .sel(and_3_out));  // open: out0

  // Notes on the sheet:
  //   Generate OpCode
  //   for load or store
  //   Stalling Logic
  //   Traverse one network per cycle
  //   Instruction fetch modified to support stalling
  //   Instruction Cache Packet
  //   Sending instruction from memory
  //   Compare Core ID to Dest ID
  //   OpCode
  //   Packet Generation
  //   Sending Out Packet
  //   Sending data from memory
  //   4 scenarios for packet in network block
  //   Check if network is free before sending new packet
  //   Data Cache Packet
  //   Core ID: 2 bits - row, 2 bits - col
  //   "Data"
  //   Return Packet: Going out bit | Dest ID | Data
  //   Memory Packet
  //   Going out packet: Going out bit | Dest ID | OpCode | Source ID | Memory Address 
  //   Routing algorithm - compare Core ID to Dest id to determine where to move
  //   Find correct row and then col
  //   +1 row
  //   -1 row
  //   +1 col
  //   -1 col
endmodule
