// Logisim project InstCache.circ as structural Verilog: 1 circuit, main circuit main
module main (
  input  [31:0] Address,
  input  Load,
  output [1:0] Byte_offset,
  output HIT_MISS,
  output [31:0] Data_Output
);

  wire Clock_out, comparator_1_eq, ram_1_data;
  wire [19:0] ram_2_data;

  Clock Clock (.out(Clock_out));
  RAM #(.addrWidth(10), .dataWidth(1)) ram_1 (
    .addr(Address[11:2]), .data(ram_1_data), .clk(Clock_out), .ld(Load));  // open: sel, clr
  and and_1 (HIT_MISS, ram_1_data, comparator_1_eq);
  RAM #(.addrWidth(10), .dataWidth(20)) ram_2 (
    .addr(Address[11:2]), .data(ram_2_data), .clk(Clock_out), .ld(Load));  // open: sel, clr
  Comparator #(.width(20)) comparator_1 (.a(ram_2_data), .b(Address[31:12]), .eq(comparator_1_eq));  // open: gt, lt
  RAM #(.addrWidth(10), .dataWidth(32)) ram_3 (
    .addr(Address[11:2]), .data(Data_Output), .clk(Clock_out), .ld(Load));  // open: sel, clr

  assign Byte_offset = Address[1:0];

  // Notes on the sheet:
  //   Tag
  //   Index
  //   VALID
  //   TAG
  //   DATA
endmodule
