// Logisim project InstFetch.circ as structural Verilog: 1 circuit, main circuit main
module main (
  input  Stall,
  input  Branch,
  input  Jump,
  input  Clock,
  input  Reset,
  input  [27:0] JumpAddress,
  input  [31:0] BranchAddress,
  output [31:0] ReadAddress
);

  wire [27:0] shifter_2_out;
  wire [31:0] adder_1_out, adder_2_out, multiplexer_1_out, multiplexer_2_out, multiplexer_3_out,
       shifter_1_out;

  Multiplexer #(.width(32), .enable("false")) multiplexer_1 (
    .in0(multiplexer_3_out), .in1(ReadAddress), .out(multiplexer_1_out), .sel(Stall));
  Register #(.width(32)) PC (.D(multiplexer_1_out), .Q(ReadAddress), .clk(Clock), .clr(Reset));  // open: en
  Adder #(.width(32)) adder_1 (.a(ReadAddress), .b(32'h4), .out(adder_1_out));  // open: cin, cout
  Shifter #(.width(32)) shifter_1 (.in(BranchAddress), .\dist (5'b00010), .out(shifter_1_out));
  Adder #(.width(32)) adder_2 (.a(adder_1_out), .b(shifter_1_out), .out(adder_2_out));  // open: cin, cout
  Multiplexer #(.width(32), .enable("false")) multiplexer_2 (
    .in0(adder_1_out), .in1(adder_2_out), .out(multiplexer_2_out), .sel(Branch));
  Shifter #(.width(28)) shifter_2 (.in(JumpAddress), .\dist (5'b00010), .out(shifter_2_out));
  Multiplexer #(.width(32), .enable("false")) multiplexer_3 (
    .in0(multiplexer_2_out), .in1({ReadAddress[31:28], shifter_2_out}), .out(multiplexer_3_out), .sel(Jump));
endmodule
