// Logisim project MultiCoreCPUNetwork.circ as structural Verilog: 1 circuit, main circuit main
module main (
);

  wire [31:0] main_1_output_east, main_1_output_south, main_2_output_east, main_2_output_north,
       main_2_output_south, main_3_output_east, main_3_output_south, main_4_output_east, main_5_output_east,
       main_6_output_east, main_7_output_east, main_8_output_east, main_9_output_east, main_10_output_east,
       main_11_output_east, main_12_output_east;

  FullCPU_main main_1 (
    .Network_Input(main_2_output_north), .Output_South(main_1_output_south),
    .Output_East(main_1_output_east), .Core_ID(4'b0000));  // open: Clock, Output_North, Output_West, Going_Out__Dest_ID
  FullCPU_main main_2 (
    .Network_Input(main_1_output_south), .Output_North(main_2_output_north),
    .Output_South(main_2_output_south), .Output_East(main_2_output_east), .Core_ID(4'b0100),
    .Going_Out__Dest_ID(5'b10000));  // open: Clock, Output_West
  FullCPU_main main_3 (
    .Network_Input(main_2_output_south), .Output_North(main_1_output_south),
    .Output_South(main_3_output_south), .Output_East(main_3_output_east), .Core_ID(4'b1000),
    .Going_Out__Dest_ID(5'b11100));  // open: Clock, Output_West
  FullCPU_main main_4 (
    .Network_Input(main_3_output_south), .Output_North(main_2_output_south),
    .Output_East(main_4_output_east), .Core_ID(4'b1100));  // open: Clock, Output_South, Output_West, Going_Out__Dest_ID
  Clock clock_1 ();  // open: out
  FullCPU_main main_5 (
    .Network_Input(main_1_output_east), .Output_South(main_2_output_east), .Output_East(main_5_output_east),
    .Output_West(main_2_output_north), .Core_ID(4'b0001), .Going_Out__Dest_ID(5'b10000));  // open: Clock, Output_North
  FullCPU_main main_6 (
    .Network_Input(main_2_output_east), .Output_North(main_1_output_east), .Output_South(main_3_output_east),
    .Output_East(main_6_output_east), .Output_West(main_1_output_south), .Core_ID(4'b0101),
    .Going_Out__Dest_ID(5'b10000));  // open: Clock
  FullCPU_main main_7 (
    .Network_Input(main_3_output_east), .Output_North(main_2_output_east), .Output_South(main_4_output_east),
    .Output_East(main_7_output_east), .Output_West(main_2_output_south), .Core_ID(4'b1001),
    .Going_Out__Dest_ID(5'b11100));  // open: Clock
  FullCPU_main main_8 (
    .Network_Input(main_4_output_east), .Output_North(main_3_output_east), .Output_East(main_8_output_east),
    .Output_West(main_3_output_south), .Core_ID(4'b1101), .Going_Out__Dest_ID(5'b11100));  // open: Clock, Output_South
  FullCPU_main main_9 (
    .Network_Input(main_5_output_east), .Output_South(main_6_output_east), .Output_East(main_9_output_east),
    .Output_West(main_1_output_east), .Core_ID(4'b0010), .Going_Out__Dest_ID({5{1'b1}}));  // open: Clock, Output_North
  FullCPU_main main_10 (
    .Network_Input(main_6_output_east), .Output_North(main_5_output_east), .Output_South(main_7_output_east),
    .Output_East(main_10_output_east), .Output_West(main_2_output_east), .Core_ID(4'b0110),
    .Going_Out__Dest_ID({5{1'b1}}));  // open: Clock
  FullCPU_main main_11 (
    .Network_Input(main_7_output_east), .Output_North(main_6_output_east), .Output_South(main_8_output_east),
    .Output_East(main_11_output_east), .Output_West(main_3_output_east), .Core_ID(4'b1010),
    .Going_Out__Dest_ID(5'b10011));  // open: Clock
  FullCPU_main main_12 (
    .Network_Input(main_8_output_east), .Output_North(main_7_output_east), .Output_East(main_12_output_east),
    .Output_West(main_4_output_east), .Core_ID(4'b1110), .Going_Out__Dest_ID(5'b10011));  // open: Clock, Output_South
  FullCPU_main main_13 (
    .Network_Input(main_9_output_east), .Output_South(main_10_output_east), .Output_West(main_5_output_east),
    .Core_ID(4'b0011));  // open: Clock, Output_North, Output_East, Going_Out__Dest_ID
  FullCPU_main main_14 (
    .Network_Input(main_10_output_east), .Output_North(main_9_output_east),
    .Output_South(main_11_output_east), .Output_West(main_6_output_east), .Core_ID(4'b0111),
    .Going_Out__Dest_ID({5{1'b1}}));  // open: Clock, Output_East
  FullCPU_main main_15 (
    .Network_Input(main_11_output_east), .Output_North(main_10_output_east),
    .Output_South(main_12_output_east), .Output_West(main_7_output_east), .Core_ID(4'b1011),
    .Going_Out__Dest_ID(5'b10011));  // open: Clock, Output_East
  FullCPU_main main_16 (
    .Network_Input(main_12_output_east), .Output_North(main_11_output_east),
    .Output_West(main_8_output_east), .Core_ID(4'b1111));  // open: Clock, Output_South, Output_East, Going_Out__Dest_ID

  // Notes on the sheet:
  //   Core IDs
  //   Going Out + Dest ID
endmodule
