// Logisim project Writeback.circ as structural Verilog: 2 circuits, main circuit Control Logic
module Control_Logic (
  input  [5:0] Opcode,
  output Jump,
  output RegDest,
  output BNE,
  output BEQ,
  output MemWrite,
  output MemRead,
  output MemToReg,
  output RegWrite,
  output ALUSrc,
  output ExtOp,
  output R_Type,
  output [3:0] ALUOp
);

  wire ADDI_out, ANDI_out, or_1_out, or_2_out, ORI_out, SLTI_out, undriven, XORI_out;

  and u_R_type (R_Type, ~Opcode[5], ~Opcode[4], ~Opcode[3], ~Opcode[2], ~Opcode[1], ~Opcode[0]);  // AND_Gate
  and LW (MemRead, Opcode[5], ~Opcode[4], ~Opcode[3], ~Opcode[2], Opcode[1], Opcode[0]);  // AND_Gate
  and SW (MemWrite, Opcode[5], ~Opcode[4], Opcode[3], ~Opcode[2], Opcode[1], Opcode[0]);  // AND_Gate
  and u_BEQ (BEQ, ~Opcode[5], ~Opcode[4], ~Opcode[3], Opcode[2], ~Opcode[1], ~Opcode[0]);  // AND_Gate
  and ADDI (ADDI_out, ~Opcode[5], ~Opcode[4], Opcode[3], ~Opcode[2], ~Opcode[1], ~Opcode[0]);  // AND_Gate
  or or_1 (or_1_out, MemRead, MemWrite, ADDI_out);
  and SLTI (SLTI_out, ~Opcode[5], ~Opcode[4], Opcode[3], ~Opcode[2], Opcode[1], ~Opcode[0]);  // AND_Gate
  or or_2 (or_2_out, BEQ, BNE);
  and ANDI (ANDI_out, ~Opcode[5], ~Opcode[4], Opcode[3], Opcode[2], ~Opcode[1], ~Opcode[0]);  // AND_Gate
  and ORI (ORI_out, ~Opcode[5], ~Opcode[4], Opcode[3], Opcode[2], ~Opcode[1], Opcode[0]);  // AND_Gate
  and XORI (XORI_out, ~Opcode[5], ~Opcode[4], Opcode[3], Opcode[2], Opcode[1], ~Opcode[0]);  // AND_Gate
  and J (Jump, ~Opcode[5], ~Opcode[4], ~Opcode[3], ~Opcode[2], Opcode[1], ~Opcode[0]);  // AND_Gate
  and u_BNE (BNE, ~Opcode[5], ~Opcode[4], ~Opcode[3], Opcode[2], ~Opcode[1], Opcode[0]);  // AND_Gate
  Priority_Encoder #(.select(4)) priority_encoder_1 (
    .in0(or_1_out), .in2(or_2_out), .in4(ANDI_out), .in5(ORI_out), .in6(XORI_out), .in7(undriven),
    .in8(undriven), .in10(SLTI_out), .out(ALUOp));  // open: in1, in3, in9, in11, in12, in13, in14, in15, gs, en_out, en_in
  or u_RegWrite (RegWrite, XORI_out, ORI_out, ANDI_out, SLTI_out, ADDI_out, MemRead, R_Type);
  nor nor_1 (ALUSrc, BNE, BEQ, R_Type);
  nor nor_2 (ExtOp, XORI_out, ORI_out, ANDI_out);

  assign MemToReg = MemRead;
  assign RegDest = R_Type;
endmodule

module ALU_Control (
  input  [3:0] MainCntrl,
  input  [5:0] Funct,
  input  in_3,
  output Sub,
  output [2:0] ALUCntrl
);

  wire ADD_out, priority_encoder_1_p1, priority_encoder_1_p2, priority_encoder_1_p3, priority_encoder_1_p6,
       priority_encoder_1_p7;
  wire [3:0] multiplexer_1_out;

  Multiplexer #(.width(4)) multiplexer_1 (
    .in0(MainCntrl), .in1(Funct[3:0]), .out(multiplexer_1_out), .sel(in_3));  // open: en
  and ADD (ADD_out, ~multiplexer_1_out[3], ~multiplexer_1_out[2], ~multiplexer_1_out[1], ~multiplexer_1_out[0]);  // AND_Gate
  // Priority_Encoder #(.select(4)) priority_encoder_1: pin names not known; wires that end beside it: priority_encoder_1_p1, priority_encoder_1_p2, priority_encoder_1_p3, ADD_out, {Sub, ALUCntrl}, priority_encoder_1_p6, priority_encoder_1_p7
  and u_SUB (priority_encoder_1_p6, ~multiplexer_1_out[3], ~multiplexer_1_out[2], multiplexer_1_out[1], ~multiplexer_1_out[0]);  // AND_Gate
  and AND (priority_encoder_1_p1, ~multiplexer_1_out[3], multiplexer_1_out[2], ~multiplexer_1_out[1], ~multiplexer_1_out[0]);  // AND_Gate
  and OR (priority_encoder_1_p2, ~multiplexer_1_out[3], multiplexer_1_out[2], ~multiplexer_1_out[1], multiplexer_1_out[0]);  // AND_Gate
  and XOR (priority_encoder_1_p3, ~multiplexer_1_out[3], multiplexer_1_out[2], multiplexer_1_out[1], ~multiplexer_1_out[0]);  // AND_Gate
  and SLT (priority_encoder_1_p7, multiplexer_1_out[3], ~multiplexer_1_out[2], multiplexer_1_out[1], ~multiplexer_1_out[0]);  // AND_Gate
endmodule
